# Fritzing sketch Diagrama Examen (saved by Fritzing 0.9.3b)
breadboards: 1

parts:
  Raspberry_Pi_2 = Raspberry Pi 3 [part_number=RPI-3-V1.2]
  LED1 = LED - 5mm [color="Red (633nm)" package="5 mm [THT]"]
  LED2 = LED - 5mm [color="White (4500K)" package="5 mm [THT]"]
  LED3 = LED - 5mm [color="Green (570nm)" package="5 mm [THT]"]
  LED4 = LED - 5mm [color="Yellow (595nm)" package="5 mm [THT]"]
  R1 = Resistor [tolerance=±5% resistance=220 package=THT]
  J1 = Piezo Speaker
  R2 = Resistor [tolerance=±5% resistance=220 package=THT]
  R3 = Resistor [tolerance=±5% resistance=220 package=THT]
  R4 = Resistor [tolerance=±5% resistance=220 package=THT]
  R5 = Resistor [tolerance=±5% resistance=220 package=THT]

nets:
  N1: Raspberry_Pi_2.GPIO2, R1.Pin_0
  N2: Raspberry_Pi_2.GPIO3, R4.Pin_0
  N3: Raspberry_Pi_2.GIPO4, R3.Pin_0
  N4: Raspberry_Pi_2.GIPO17, R2.Pin_0
  N5: Raspberry_Pi_2.GIPO27, R5.Pin_0
  N6: Raspberry_Pi_2.GND, LED1.cathode, LED2.cathode, LED3.cathode, LED4.cathode, J1.pin1
  N7: LED1.anode, R2.Pin_1
  N8: LED2.anode, R1.Pin_1
  N9: LED3.anode, R3.Pin_1
  N10: LED4.anode, R4.Pin_1
  N11: J1.pin2, R5.Pin_1
