# Fritzing sketch Diagrama1 (saved by Fritzing 0.9.3b)
breadboards: 1

parts:
  VCC1 = Battery block 9V
  R3 = Rotary Potentiometer (Small) [maximum_resistance=10kΩ package=THT]
  C1 = Electrolytic Capacitor [capacitance=0.1µF package="100 mil [THT, electrolytic]"]
  Q1 = NPN-Transistor [package="TO92 [THT]"]
  D1 = Rectifier Diode [part_number=1N4001 package="300 mil [THT]"]
  U1 = 555 Timer [package="DIP8 [THT]"]
  M1 = DC Motor
  R4 = Resistor [tolerance=±5% resistance=1k package=THT]
  R5 = Resistor [tolerance=±5% resistance=1k package=THT]

nets:
  N1: VCC1.-, C1.-, Q1.E, U1.Ground
  N2: VCC1.+, D1.cathode, U1.Reset, U1.Vcc_Supply_Voltage, M1.pin_1, R4.Pin_0
  N3: R3.wiper, C1.+, U1.Trigger, U1.Threshold
  N4: R3.leg2, U1.Discharge, R4.Pin_1
  N5: Q1.B, R5.Pin_0
  N6: Q1.C, D1.anode, M1.pin_2
  N7: U1.Output, R5.Pin_1
