# Fritzing sketch Practica3 (saved by Fritzing 0.9.3b)
breadboards: 1

parts:
  Raspberry_Pi_2 = Raspberry Pi 3 [part_number=RPI-3-V1.2]
  S1 = Pushbutton [package=THT]
  LED1 = LED - 5mm [color="Red (633nm)" package="5 mm [THT]"]
  J1 = Piezo Speaker
  R1 = Resistor [tolerance=±5% resistance=220 package=THT]
  R2 = Resistor [tolerance=±5% resistance=220 package=THT]
  R3 = Resistor [tolerance=±5% resistance=10k package=THT]

nets:
  N1: Raspberry_Pi_2.3v3, S1.leg1
  N2: Raspberry_Pi_2.GND, R1.Pin_1, R2.Pin_1, R3.Pin_1
  N3: Raspberry_Pi_2.GPIO18, S1.leg0, R3.Pin_0
  N4: Raspberry_Pi_2.GPIO14, LED1.anode
  N5: LED1.cathode, R1.Pin_0
  N6: J1.pin1, R2.Pin_0
