# Fritzing sketch Practica4 (saved by Fritzing 0.9.3b)
breadboards: 1

parts:
  R1 = Resistor [tolerance=±5% resistance=220 package=THT]
  J1 = Piezo Speaker
  Raspberry_Pi_1 = Raspberry Pi 3 [part_number=RPI-3-V1.2]
  hc-sr1 = hc-sr04
  R2 = Resistor [tolerance=±5% resistance=220 package=THT]
  R3 = Resistor [tolerance=±5% resistance=220 package=THT]
  R4 = Resistor [tolerance=±5% resistance=220 package=THT]
  R5 = Resistor [tolerance=±5% resistance=10k package=THT]
  R6 = Resistor [tolerance=±5% resistance=220 package=THT]
  LED1 = LED - 5mm [color="Red (633nm)" package="5 mm [THT]"]
  LED2 = LED - 5mm [color="Green (555nm)" package="5 mm [THT]"]
  LED3 = LED - 5mm [color="White (8000K)" package="5 mm [THT]"]
  LED4 = LED - 5mm [color="Yellow (592nm)" package="5 mm [THT]"]
  LED5 = LED - 5mm [color="Blue (430nm)" package="5 mm [THT]"]

nets:
  N1: R1.Pin_0, Raspberry_Pi_1.GPIO16
  N2: R1.Pin_1, LED1.anode
  GND: J1.pin1, Raspberry_Pi_1.GND, hc-sr1.GND, LED1.cathode, LED2.cathode, LED3.cathode, LED4.cathode, LED5.cathode
  N3: J1.pin2, R5.Pin_1
  N4: Raspberry_Pi_1.GPIO5, R2.Pin_0
  N5: Raspberry_Pi_1.GPIO6, R5.Pin_0
  N6: Raspberry_Pi_1.GPIO13, R3.Pin_0
  N7: Raspberry_Pi_1.GPIO19, R4.Pin_0
  N8: Raspberry_Pi_1.GPIO26, R6.Pin_0
  N9: Raspberry_Pi_1.GPIO18, hc-sr1.Echo
  N10: Raspberry_Pi_1.GPIO15, hc-sr1.Trig
  5V: Raspberry_Pi_1.5V, hc-sr1.VCC
  N11: R2.Pin_1, LED3.anode
  N12: R3.Pin_1, LED5.anode
  N13: R4.Pin_1, LED4.anode
  N14: R6.Pin_1, LED2.anode
